# Fritzing sketch smart door lock circuit diagram (saved by Fritzing 0.9.3b)
breadboards: 2

parts:
  Gizwits_WiFi_Witty_ESP-12F1 = Gizwits WiFi Witty ESP-12F
  Part3 = RFID-RC522-v2
  M1 = 1 chan 5v relay module
  LED1 = LED - 5mm [color="Red (633nm)" package="5 mm [THT]"]
  VCC1 = Battery
  Part1 = Arduino Uno (Rev3)

nets:
  VCC: Gizwits_WiFi_Witty_ESP-12F1.VCC, M1.pin_1, Part1.5V
  GND: Gizwits_WiFi_Witty_ESP-12F1.GND, Part3.GND, M1.pin_2, Part1.GND
  N1: Gizwits_WiFi_Witty_ESP-12F1.RXD, Part1.D0/RX
  N2: Gizwits_WiFi_Witty_ESP-12F1.TXD, Part1.D1/TX
  N3: Part3.SDA, Part1.D10_PWM/SS
  N4: Part3.SCK, Part1.D13/SCK
  N5: Part3.MOSI, Part1.D11_PWM/MOSI
  N6: Part3.MISO, Part1.D12/MISO
  N7: Part3.3_3V, Part1.3V3
  N8: M1.pin_3, Part1.D7
  N9: M1.pin_5, VCC1.+
  N10: M1.pin_6, LED1.anode
  N11: LED1.cathode, VCC1.-

notes:
  refrence to 12v solenoid

custom parts:
  RFID-RC522-v2: A simple China made RFID-RC522 Reader; do check the pin labels, as this is a MFRC522 based clone.
  1 chan 5v relay module: 1 Channel 5V Relay Module Board Shield with Optocoupler Support High and Low Level Trigger for Arduino.
